# Fritzing sketch tamaguino-no-resistors (saved by Fritzing 0.9.2b)
breadboards: 1

parts:
  Grove1 = Grove OLED 128x96
  S1 = Pushbutton [package="[THT]"]
  S2 = Pushbutton [package="[THT]"]
  S3 = Pushbutton [package="[THT]"]
  J1 = Piezo Speaker
  Part1 = Arduino Uno (Rev3) - ICSP

nets:
  GND: Grove1.GND, S1.Pin_3, S1.Pin_4, S2.Pin_3, S2.Pin_4, S3.Pin_3, S3.Pin_4, J1.pin1, Part1.GND
  VCC: Grove1.VCC, S1.Pin_1, S1.Pin_2, S2.Pin_1, S2.Pin_2, Part1.D8, Part1.D9_PWM, Part1.3V3
  N1: Grove1.SDA, Part1.A4/SDA
  N2: Grove1.SCL, Part1.A5/SCL
  N3: S3.Pin_1, S3.Pin_2, Part1.D7
  N4: J1.pin2, Part1.D6_PWM
