# Fritzing sketch tamaguino (saved by Fritzing 0.9.2b)
circuit board: 8.46667cm x 5.64444cm
breadboards: 1

parts:
  Grove1 = Grove OLED 128x96
  S1 = Pushbutton [package="[THT]"]
  S2 = Pushbutton [package="[THT]"]
  S3 = Pushbutton [package="[THT]"]
  J1 = Piezo Speaker
  R1 = Resistor [tolerance=±5% resistance=220 package=THT]
  R2 = Resistor [tolerance=±5% resistance=220 package=THT]
  R3 = Resistor [tolerance=±5% resistance=220 package=THT]
  Part1 = Arduino Uno (Rev3) - ICSP

nets (from the breadboard view):
  GND: Grove1.GND, J1.pin1, R1.Pin_1, R2.Pin_1, R3.Pin_1, Part1.GND
  VCC: Grove1.VCC, S1.Pin_1, S1.Pin_2, S2.Pin_1, S2.Pin_2, S3.Pin_1, S3.Pin_2, Part1.3V3
  N1: Grove1.SDA, Part1.A4/SDA
  N2: Grove1.SCL, Part1.A5/SCL
  N3: S1.Pin_3, S1.Pin_4, R1.Pin_0, Part1.D9_PWM
  N4: S2.Pin_3, S2.Pin_4, R2.Pin_0, Part1.D8
  N5: S3.Pin_3, S3.Pin_4, R3.Pin_0, Part1.D7
  N6: J1.pin2, Part1.D6_PWM
